// Logisim project Increment A.circ as structural Verilog: 1 circuit, main circuit main
module main (
  input  A0,
  input  A1,
  input  A2,
  output _0,
  output _1,
  output _2,
  output _3
);

  wire half_adder_1_p4, half_adder_2_p4;

  // Half_adder half_adder_1: pin names not known; wires that end beside it: 1'b1, A0, _0, half_adder_1_p4
  // Half_adder half_adder_2: pin names not known; wires that end beside it: half_adder_1_p4, A1, _1, half_adder_2_p4
  // Half_adder half_adder_3: pin names not known; wires that end beside it: half_adder_2_p4, A2, _2, _3
endmodule
